// Logisim project 01-AC-A-ProcesadorSimpleBase.circ as structural Verilog: 5 circuits, main circuit main
module main (
  input  [15:0] Number_to_evaluate,
  input  InsertNumber,
  input  Clear,
  input  Clear_2,
  input  SaveNumber,
  input  Clear_3
);

  wire ADDI, ALUope, and_1_out, and_2_out, B, BEQ, BLT, clk, CTO, Igual, LDR, Menor, or_1_out, or_2_out,
       or_3_out, or_4_out, or_5_out, or_7_out, or_8_out, or_9_out, STR;
  wire [1:0] multiplexer_6_out;
  wire [2:0] br_1_tmp, MEMDAT_rf, multiplexer_2_out;
  wire [15:0] adder_1_out, ALU, bit_extender_1_out, bit_extender_2_out, bit_extender_3_out,
       multiplexer_1_out, multiplexer_3_out, multiplexer_4_out, multiplexer_5_out, multiplexer_7_out,
       multiplexer_8_out, multiplexer_9_out, multiplexer_10_out, PC, ram_1_data, ram_2_data, rd, rf;

  and and_1 (and_1_out, BEQ, Igual);
  and and_2 (and_2_out, BLT, Menor);
  Register #(.width(16)) u_PC (.D(multiplexer_1_out), .en(1'b1), .Q(PC), .clk(clk), .clr(Clear_3));
  Clock clock_1 (.out(clk));
  Multiplexer #(.width(16), .enable("false")) multiplexer_1 (
    .in0(adder_1_out), .in1(ALU), .out(multiplexer_1_out), .sel(or_1_out));
  or or_1 (or_1_out, B, and_1_out, and_2_out);
  Adder #(.width(16)) adder_1 (.a(16'h1), .b(PC), .out(adder_1_out));  // open: cin, cout
  // Probe on PC
  RAM #(.dataWidth(16), .bus("separate")) ram_1 (
    .addr(PC[7:0]), .data({ram_1_data[15:13], MEMDAT_rf, ram_1_data[9:0]}));  // open: din, str, sel, clk, ld, clr
  // Probe on {ram_1_data[15:13], MEMDAT_rf, ram_1_data[9:0]}
  and and_3 (ALUope, ~ram_1_data[13], ~ram_1_data[14], ~ram_1_data[15]);  // AND_Gate
  Multiplexer #(.width(3), .enable("false")) multiplexer_2 (
    .in0(ram_1_data[6:4]), .in1(ram_1_data[9:7]), .out(multiplexer_2_out), .sel(or_2_out));
  or or_2 (or_2_out, ADDI, LDR);
  and and_4 (ADDI, ram_1_data[13], ~ram_1_data[14], ~ram_1_data[15]);  // AND_Gate
  or or_3 (or_3_out, ALUope, ADDI, LDR);
  assign bit_extender_1_out = {{9{ram_1_data[6]}}, ram_1_data[6:0]};  // Bit_Extender bit_extender_1
  assign bit_extender_2_out = {{3{MEMDAT_rf[2]}}, {MEMDAT_rf, ram_1_data[9:0]}};  // Bit_Extender bit_extender_2
  and and_5 (LDR, ~ram_1_data[13], ram_1_data[14], ~ram_1_data[15]);  // AND_Gate
  BR br_1 (
    .DA(MEMDAT_rf), .DB(ram_1_data[9:7]), .DC(multiplexer_2_out), .C(multiplexer_10_out), .A(rf), .B(rd),
    .wr(or_3_out), .clk(clk), .reset(Clear), .TMP(br_1_tmp));
  // Probe on br_1_tmp
  and and_6 (STR, ram_1_data[13], ram_1_data[14], ~ram_1_data[15]);  // AND_Gate
  and and_7 (B, ~ram_1_data[13], ram_1_data[14], ram_1_data[15]);  // AND_Gate
  Multiplexer #(.width(16), .enable("false")) multiplexer_3 (
    .in0(rd), .in1(bit_extender_1_out), .out(multiplexer_3_out), .sel(or_4_out));
  or or_4 (or_4_out, BEQ, BLT, ADDI);
  and and_8 (BEQ, ~ram_1_data[13], ~ram_1_data[14], ram_1_data[15]);  // AND_Gate
  and and_9 (BLT, ram_1_data[13], ~ram_1_data[14], ram_1_data[15]);  // AND_Gate
  Multiplexer #(.width(16), .enable("false")) multiplexer_4 (.in0(rf), .in1(PC), .out(multiplexer_4_out), .sel(CTO));
  Multiplexer #(.width(16), .enable("false")) multiplexer_5 (
    .in0(multiplexer_3_out), .in1(bit_extender_2_out), .out(multiplexer_5_out), .sel(B));
  or or_5 (or_5_out, ADDI, CTO);
  Multiplexer #(.width(2), .enable("false")) multiplexer_6 (
    .in0(ram_1_data[1:0]), .in1(2'b00), .out(multiplexer_6_out), .sel(or_5_out));
  Comparator #(.width(16)) comparator_1 (.a(rf), .b(rd), .eq(Igual), .lt(Menor));  // open: gt
  or or_6 (CTO, B, BEQ, BLT);
  Multiplexer #(.width(16), .enable("false")) multiplexer_7 (
    .in0(rf), .in1(bit_extender_3_out), .out(multiplexer_7_out), .sel(or_7_out));
  assign bit_extender_3_out = {{13{MEMDAT_rf[2]}}, MEMDAT_rf};  // Bit_Extender bit_extender_3
  or or_7 (or_7_out, LDR, STR);
  ALU alu_1 (.A(multiplexer_4_out), .B(multiplexer_5_out), .OUT(ALU), .Op(multiplexer_6_out));
  Multiplexer #(.width(16), .enable("false")) multiplexer_8 (
    .in0(multiplexer_7_out), .in1(16'h1), .out(multiplexer_8_out), .sel(InsertNumber));
  Multiplexer #(.width(16), .enable("false")) multiplexer_9 (
    .in0(rd), .in1(Number_to_evaluate), .out(multiplexer_9_out), .sel(InsertNumber));
  Multiplexer #(.width(16), .enable("false")) multiplexer_10 (
    .in0(ALU), .in1(ram_2_data), .out(multiplexer_10_out), .sel(LDR));
  or or_8 (or_8_out, SaveNumber, clk);
  or or_9 (or_9_out, InsertNumber, STR);
  RAM #(.dataWidth(16), .bus("separate")) ram_2 (
    .addr(multiplexer_8_out[7:0]), .din(multiplexer_9_out), .data(ram_2_data), .str(or_9_out),
    .clk(or_8_out), .clr(Clear_2));  // open: sel, ld

  // Other names for the same wires on the sheet: EvNumber[15:0] = Number_to_evaluate; InsNumber = InsertNumber

  // Notes on the sheet:
  //   MEMINST
  //   OPCODE
  //   rf
  //   re
  //   rd
  //   MEMDAT
endmodule

module BR (
  input  wr,
  input  clk,
  input  reset,
  input  [2:0] DA,
  input  [2:0] DB,
  input  [2:0] DC,
  input  [15:0] C,
  output [15:0] A,
  output [15:0] B,
  output [2:0] TMP
);

  wire decoder_1_out1, decoder_1_out2, decoder_1_out3, decoder_1_out4, decoder_1_out5, decoder_1_out6,
       decoder_1_out7;
  wire [15:0] register_1_q, register_2_q, register_3_q, register_4_q, register_5_q, register_6_q,
       register_7_q;

  Decoder #(.select(3), .disabled(0)) decoder_1 (
    .out1(decoder_1_out1), .out2(decoder_1_out2), .out3(decoder_1_out3), .out4(decoder_1_out4),
    .out5(decoder_1_out5), .out6(decoder_1_out6), .out7(decoder_1_out7), .sel(DC), .en(wr));  // open: out0
  Register #(.width(16)) register_1 (.D(C), .en(decoder_1_out1), .Q(register_1_q), .clk(clk), .clr(reset));
  Register #(.width(16)) register_2 (.D(C), .en(decoder_1_out2), .Q(register_2_q), .clk(clk), .clr(reset));
  Register #(.width(16)) register_3 (.D(C), .en(decoder_1_out3), .Q(register_3_q), .clk(clk), .clr(reset));
  Register #(.width(16)) register_4 (.D(C), .en(decoder_1_out4), .Q(register_4_q), .clk(clk), .clr(reset));
  Register #(.width(16)) register_5 (.D(C), .en(decoder_1_out5), .Q(register_5_q), .clk(clk), .clr(reset));
  Register #(.width(16)) register_6 (.D(C), .en(decoder_1_out6), .Q(register_6_q), .clk(clk), .clr(reset));
  Register #(.width(16)) register_7 (.D(C), .en(decoder_1_out7), .Q(register_7_q), .clk(clk), .clr(reset));
  Multiplexer #(.select(3), .width(16), .enable("false")) multiplexer_1 (
    .in0({16{1'b0}}), .in1(register_1_q), .in2(register_2_q), .in3(register_3_q), .in4(register_4_q),
    .in5(register_5_q), .in6(register_6_q), .in7(register_7_q), .out(A), .sel(DA));
  Multiplexer #(.select(3), .width(16), .enable("false")) multiplexer_2 (
    .in0({16{1'b0}}), .in1(register_1_q), .in2(register_2_q), .in3(register_3_q), .in4(register_4_q),
    .in5(register_5_q), .in6(register_6_q), .in7(register_7_q), .out(B), .sel(DB));

  assign TMP = DC;
endmodule

module ALU (
  input  [1:0] Op,
  input  [15:0] A,
  input  [15:0] B,
  output [15:0] OUT
);

  wire [15:0] adder_1_out, and_1_out, divider_1_rem, or_1_out;

  Adder #(.width(16)) adder_1 (.a(A), .b(B), .out(adder_1_out));  // open: cin, cout
  Divider #(.width(16)) divider_1 (.a(A), .b(B), .rem(divider_1_rem));  // open: out, upper
  assign and_1_out = A & B;  // AND_Gate and_1, 16 bits wide
  assign or_1_out = A | B;  // OR_Gate or_1, 16 bits wide
  Multiplexer #(.select(2), .width(16), .enable("false")) multiplexer_1 (
    .in0(adder_1_out), .in1(divider_1_rem), .in2(and_1_out), .in3(or_1_out), .out(OUT), .sel(Op));
endmodule

module MEMDAT (
  input  [15:0] ADDR,
  input  [15:0] DATAIN,
  input  wr,
  input  clk,
  input  reset,
  output [15:0] DATAOUT
);

  RAM #(.dataWidth(16), .bus("separate")) ram_1 (
    .addr(ADDR[7:0]), .din(DATAIN), .data(DATAOUT), .str(wr), .clk(clk), .clr(reset));  // open: sel, ld
endmodule

module MEMINST (
  input  [15:0] in_1,
  output [15:0] out_2,
  output [15:0] out_3
);

  RAM #(.dataWidth(16), .bus("separate")) ram_1 (.addr(in_1[7:0]), .data(out_2));  // open: din, str, sel, clk, ld, clr

  assign out_3 = in_1;
endmodule
